// Logisim project Circuit.circ as structural Verilog
module FrameGraphics (
  input  RefreshScreen,
  input  Reset,
  input  [11:0] VRAM_Address,
  input  Write_VRAM,
  input  Clock,
  input  [23:0] PixelData,
  output ScreenClock,
  output Writing,
  output Clear,
  output [5:0] X,
  output [5:0] Y,
  output [23:0] Color
);

  wire and_1_out, and_2_out, or_1_out, or_2_out, s_r_ff_1_qn, ScreenX_carry, ScreenY_carry;
  wire [6:6] ScreenX_q, ScreenY_q;
  wire [11:0] register_1_q;

  and and_1 (and_1_out, ~Writing, RefreshScreen);  // AND_Gate
  S_R_Flip_Flop s_r_ff_1 (.Q(Writing), .reset(or_1_out), .Qn(s_r_ff_1_qn), .preset(and_1_out));  // open: S, R, clk
  or or_1 (or_1_out, Reset, ScreenY_carry);
  Register #(.width(12)) register_1 (.D(VRAM_Address), .en(Writing), .clk(Writing), .Q(register_1_q));  // open: clr
  or or_2 (or_2_out, s_r_ff_1_qn, Reset);
  RAM #(.addrWidth(24), .dataWidth(24)) VRAM (
    .addr({register_1_q, Y, X}), .we(and_2_out), .oe(Writing), .clk(Clock), .din(PixelData), .dout(Color));
  and and_2 (and_2_out, Write_VRAM, ~Writing);  // AND_Gate
  Counter #(.max('h42), .width(7)) ScreenX (
    .clr(or_2_out), .load(1'b0), .up(1'b1), .count(Writing), .clk(Clock), .carry(ScreenX_carry),
    .Q({ScreenX_q[6], X}));  // open: D
  Counter #(.max('h42), .width(7)) ScreenY (
    .clr(or_2_out), .load(1'b0), .up(1'b1), .count(ScreenX_carry), .clk(Clock), .carry(ScreenY_carry),
    .Q({ScreenY_q[6], Y}));  // open: D

  assign Clear = Reset;
  assign ScreenClock = Clock;
endmodule

module main (
  input  [15:0] in_1,
  input  [1:0] in_2,
  output [3:0] out_3
);

  wire and_1_out, and_2_out, and_3_out, and_4_out, and_5_out, and_6_out, and_7_out, and_8_out, and_9_out,
       and_10_out, and_11_out, and_12_out, and_13_out, and_14_out, and_15_out, and_16_out, button_1_out,
       clock_1_out, counter_1_carry, counter_2_carry, counter_3_carry, counter_4_carry, counter_5_carry,
       counter_6_carry, decoder_1_out0, decoder_1_out1, decoder_2_out6, decoder_3_out1, decoder_3_out2,
       decoder_3_out3, not_2_out, not_3_out, not_4_out, not_5_out, not_6_out, or_1_out, or_2_out, or_4_out,
       or_5_out, or_6_out, or_7_out, or_8_out, or_9_out, or_10_out, or_11_out, or_12_out, or_13_out,
       or_14_out, or_15_out, or_16_out, or_17_out, or_18_out, or_19_out, or_20_out, or_21_out, or_22_out,
       pla_1_out, por_1_out, pull_resistor_2_node, pull_resistor_4_node, risingedgetrigger_1_out_2,
       s_r_ff_1_q, s_r_ff_2_q, s_r_ff_2_qn, s_r_ff_3_q, s_r_ff_4_q, s_r_ff_5_q, s_r_ff_5_qn, s_r_ff_6_q,
       s_r_ff_7_q, s_r_ff_7_qn, s_r_ff_8_q, s_r_ff_9_q, s_r_ff_9_qn, s_r_ff_10_q, s_r_ff_11_q, s_r_ff_11_qn,
       s_r_ff_12_q, s_r_ff_13_q, s_r_ff_13_qn, shift_register_1_p1, shift_register_1_p3, shift_register_1_p4;
  wire [0:0] pull_resistor_3_node;
  wire [1:1] ALU_OA_q_2;
  wire [2:0] demultiplexer_1_out0;
  wire [3:0] bitselector_2_out, demultiplexer_1_out1, demultiplexer_1_out2, demultiplexer_1_out3,
       demultiplexer_1_out4, demultiplexer_1_out5, demultiplexer_1_out6, demultiplexer_1_out7,
       multiplexer_1_out, shift_register_1_p6;
  wire [4:0] decoder_4_out0, demultiplexer_2_out1, or_23_out, pull_resistor_6_node, pull_resistor_7_node,
       pull_resistor_16_node;
  wire [8:4] shift_register_1_p6_2;
  wire [9:0] decoder_5_out1;
  wire [11:0] decoder_6_out1;
  wire [19:0] stateregister_1_q;
  wire [23:0] counter_1_q, counter_2_q, counter_3_q, counter_4_q, counter_5_q, counter_6_q;
  wire [30:0] ALU_OA_q;
  wire [31:0] alu_1_outa, alu_1_outb, ALU_A_q, ALU_B_q, ALU_C_q, controlled_buffer_1_out, ram_1_dout,
       RAM_Addr_q;
  wire [32:0] controlled_buffer_6_out;
  wire [35:0] controlled_buffer_3_out, Interupt_GPU_data, Interupt_X1_data, Interupt_X2_data,
       Interupt_X3_data, Interupt_X4_data, Main_data, register_1_q;
  wire [62:0] rom_1_data;

  S_R_Flip_Flop s_r_ff_1 (
    .S(s_r_ff_2_qn), .R(1'b0), .clk(shift_register_1_p4), .Q(s_r_ff_1_q), .reset(or_2_out));  // open: Qn, preset
  ROM #(.addrWidth(4), .dataWidth(63)) rom_1 (.addr(register_1_q[35:32]), .data(rom_1_data));
  Register #(.trigger("falling"), .width(36)) register_1 (
    .D(controlled_buffer_3_out), .en(s_r_ff_1_q), .clk(shift_register_1_p4), .Q(register_1_q), .clr(or_1_out));
  assign controlled_buffer_1_out = decoder_1_out0 ? register_1_q[31:0] : 32'bz;  // Controlled_Buffer controlled_buffer_1
  or or_1 (or_1_out, shift_register_1_p1, risingedgetrigger_1_out_2);
  S_R_Flip_Flop s_r_ff_2 (
    .S(s_r_ff_1_q), .R(and_1_out), .clk(shift_register_1_p4), .Q(s_r_ff_2_q), .reset(shift_register_1_p1),
    .Qn(s_r_ff_2_qn));  // open: preset
  and and_1 (and_1_out, ~s_r_ff_1_q, and_5_out);  // AND_Gate
  PLA #(.in_width(4), .out_width(1), .\table ("1111 1 # HLT")) pla_1 (.in(register_1_q[35:32]), .out(pla_1_out));
  or or_2 (or_2_out, s_r_ff_2_q, shift_register_1_p1);
  // Shift_Register #(.length(7), .width(9)) shift_register_1: pin names not known; wires that end beside it: shift_register_1_p1, s_r_ff_2_qn, shift_register_1_p3, shift_register_1_p4, {9{1'b0}}, {shift_register_1_p6_2, shift_register_1_p6}
  not not_1 (shift_register_1_p3, s_r_ff_2_qn);
  Pull_Resistor pull_resistor_1 (.node(shift_register_1_p4));
  Clock clock_1 (.out(clock_1_out));
  assign shift_register_1_p4 = s_r_ff_3_q ? clock_1_out : 1'bz;  // Controlled_Buffer controlled_buffer_2
  POR por_1 (.out(por_1_out));
  Button button_1 (.out(button_1_out));
  RisingEdgeTrigger risingedgetrigger_1 (.out_2(risingedgetrigger_1_out_2), .in_1(and_5_out));
  Pull_Resistor pull_resistor_2 (.node(pull_resistor_2_node));
  and and_2 (and_2_out, pull_resistor_2_node, ~or_4_out);  // AND_Gate
  or or_3 (shift_register_1_p1, por_1_out, button_1_out);
  and and_3 (and_3_out, and_4_out, ~or_4_out);  // AND_Gate
  Counter #(.max('hffffff), .width(24)) counter_1 (
    .clr(shift_register_1_p1), .load(and_2_out), .up(1'b1), .count(and_3_out), .clk(shift_register_1_p4),
    .D(controlled_buffer_1_out[31:8]), .carry(counter_1_carry), .Q(counter_1_q));
  ROM #(.addrWidth(24), .dataWidth(36)) Main (.addr(counter_1_q), .data(Main_data));
  BitSelector #(.group(4), .width(16)) bitselector_1 (.in(in_1), .out(out_3), .sel(in_2));
  S_R_Flip_Flop s_r_ff_3 (
    .S(1'b1), .R(1'b0), .clk(button_1_out), .Q(s_r_ff_3_q), .reset(or_5_out));  // open: Qn, preset
  or or_4 (or_4_out, or_7_out, or_9_out);
  Pull_Resistor pull_resistor_3 (.node(pull_resistor_3_node[0]));
  or or_5 (or_5_out, pla_1_out, counter_1_carry);
  and and_4 (and_4_out, s_r_ff_2_q, and_5_out);
  not not_2 (not_2_out, or_4_out);
  Pull_Resistor pull_resistor_4 (.node(pull_resistor_4_node));
  and and_5 (and_5_out, pull_resistor_4_node, or_6_out);
  or or_6 (or_6_out, ~pull_resistor_3_node[0], ALU_OA_q_2[1]);  // OR_Gate
  and and_6 (and_6_out, pull_resistor_2_node, or_23_out[0]);
  or or_7 (or_7_out, or_11_out, s_r_ff_5_q);
  assign controlled_buffer_3_out = not_2_out ? Main_data : 36'bz;  // Controlled_Buffer controlled_buffer_3
  Decoder #(.enable("false"), .select(4)) decoder_1 (
    .out0(decoder_1_out0), .out1(decoder_1_out1), .sel(stateregister_1_q[15:12]));  // open: out2, out3, out4, out5, out6, out7, out8, out9, out10, out11, out12, out13, out14, out15
  Pull_Resistor pull_resistor_5 (.node(stateregister_1_q[15:12]));
  Pull_Resistor pull_resistor_6 (.node(pull_resistor_6_node));
  Demultiplexer #(.select(3), .tristate("true"), .width(4)) demultiplexer_1 (
    .out0({demultiplexer_1_out0, pull_resistor_3_node[0]}), .out1(demultiplexer_1_out1),
    .out2(demultiplexer_1_out2), .out3(demultiplexer_1_out3), .out4(demultiplexer_1_out4),
    .out5(demultiplexer_1_out5), .out6(demultiplexer_1_out6), .out7(demultiplexer_1_out7),
    .in(multiplexer_1_out), .sel(shift_register_1_p6_2[8:6]));
  Decoder #(.enable("false"), .select(3)) decoder_2 (
    .out0(pull_resistor_4_node), .out1(pull_resistor_6_node[0]), .out2(pull_resistor_6_node[1]),
    .out3(pull_resistor_6_node[2]), .out4(pull_resistor_6_node[3]), .out5(pull_resistor_6_node[4]),
    .out6(decoder_2_out6), .sel(shift_register_1_p6_2[8:6]));  // open: out7
  Multiplexer #(.width(4)) multiplexer_1 (
    .in0(shift_register_1_p6), .in1(bitselector_2_out), .out(multiplexer_1_out),
    .sel(shift_register_1_p6_2[4]));
  or or_8 (or_8_out, shift_register_1_p1, s_r_ff_5_qn);
  Counter #(.max('hffffff), .width(24)) counter_2 (
    .clr(or_8_out), .load(and_6_out), .up(1'b1), .count(s_r_ff_5_q), .clk(shift_register_1_p4),
    .D(controlled_buffer_1_out[31:8]), .carry(counter_2_carry), .Q(counter_2_q));
  ROM #(.addrWidth(24), .dataWidth(36)) Interupt_GPU (.addr(counter_2_q), .data(Interupt_GPU_data));
  Decoder #(.enable("false"), .select(4), .tristate("true")) decoder_3 (
    .out1(decoder_3_out1), .out2(decoder_3_out2), .out3(decoder_3_out3), .out4(pull_resistor_2_node),
    .sel(stateregister_1_q[11:8]));  // open: out0, out5, out6, out7, out8, out9, out10, out11, out12, out13, out14, out15
  BitSelector #(.group(4), .width(32)) bitselector_2 (
    .in(controlled_buffer_1_out), .out(bitselector_2_out), .sel({2'b00, shift_register_1_p6_2[5]}));
  Decoder #(.enable("false"), .select(3)) decoder_4 (
    .out0(decoder_4_out0[0]), .out1(decoder_4_out0[1]), .out2(decoder_4_out0[2]), .out3(decoder_4_out0[3]),
    .out4(decoder_4_out0[4]), .sel(demultiplexer_1_out7[2:0]));  // open: out5, out6, out7
  Pull_Resistor pull_resistor_7 (.node(pull_resistor_7_node));
  or or_9 (or_9_out, or_13_out, s_r_ff_4_q);
  S_R_Flip_Flop s_r_ff_4 (
    .S(pull_resistor_7_node[0]), .clk(pull_resistor_7_node[0]), .Q(s_r_ff_4_q), .reset(or_23_out[0]));  // open: R, Qn, preset
  S_R_Flip_Flop s_r_ff_5 (
    .S(or_23_out[0]), .R(1'b0), .clk(or_23_out[0]), .Q(s_r_ff_5_q), .reset(counter_2_carry), .Qn(s_r_ff_5_qn));  // open: preset
  Decoder #(.enable("false"), .select(4), .tristate("true")) decoder_5 (
    .out1(decoder_5_out1[0]), .out2(decoder_5_out1[1]), .out3(decoder_5_out1[2]), .out4(decoder_5_out1[3]),
    .out5(decoder_5_out1[4]), .out6(decoder_5_out1[5]), .out7(decoder_5_out1[6]), .out8(decoder_5_out1[7]),
    .out9(decoder_5_out1[8]), .out10(decoder_5_out1[9]), .sel(stateregister_1_q[7:4]));  // open: out0, out11, out12, out13, out14, out15
  Decoder #(.enable("false"), .select(4), .tristate("true")) decoder_6 (
    .out1(decoder_6_out1[0]), .out2(decoder_6_out1[1]), .out3(decoder_6_out1[2]), .out4(decoder_6_out1[3]),
    .out5(decoder_6_out1[4]), .out6(decoder_6_out1[5]), .out7(controlled_buffer_6_out[32]),
    .out8(decoder_6_out1[7]), .out9(decoder_6_out1[8]), .out10(decoder_6_out1[9]),
    .out11(decoder_6_out1[10]), .out12(decoder_6_out1[11]), .sel(stateregister_1_q[3:0]));  // open: out0, out13, out14, out15
  StateRegister stateregister_1 (
    .Q(stateregister_1_q), .Reset(or_10_out), .Clock(shift_register_1_p4),
    .Data({demultiplexer_1_out5, demultiplexer_1_out4, demultiplexer_1_out3, demultiplexer_1_out2, demultiplexer_1_out1}),
    .Selector(pull_resistor_6_node));
  or or_10 (or_10_out, and_5_out, shift_register_1_p1);
  Demultiplexer #(.width(5)) demultiplexer_2 (
    .out0(pull_resistor_7_node), .out1(demultiplexer_2_out1), .in(decoder_4_out0),
    .sel(demultiplexer_1_out7[3]));
  Pull_Resistor pull_resistor_8 (.node(demultiplexer_2_out1));
  not not_3 (not_3_out, s_r_ff_5_q);
  Pull_Resistor pull_resistor_9 (.node(decoder_5_out1));
  and and_7 (and_7_out, decoder_1_out1, decoder_6_out1[7]);
  assign controlled_buffer_1_out = and_7_out ? controlled_buffer_6_out[31:0] : 32'bz;  // Controlled_Buffer controlled_buffer_4
  and and_8 (and_8_out, decoder_3_out3, decoder_5_out1[7]);
  Pull_Resistor pull_resistor_10 (.node(decoder_3_out1));
  or or_11 (or_11_out, or_14_out, s_r_ff_7_q);
  assign controlled_buffer_3_out = s_r_ff_5_q ? Interupt_GPU_data : 36'bz;  // Controlled_Buffer controlled_buffer_5
  assign controlled_buffer_6_out[31:0] = and_8_out ? controlled_buffer_1_out : 32'bz;  // Controlled_Buffer controlled_buffer_6
  Register #(.trigger("falling"), .width(32)) RAM_Addr (
    .D(controlled_buffer_1_out), .en(decoder_3_out1), .clk(shift_register_1_p4), .Q(RAM_Addr_q));  // open: clr
  Pull_Resistor pull_resistor_11 (.node(RAM_Addr_q[31:24]));
  and and_9 (and_9_out, pull_resistor_2_node, or_23_out[1]);
  and and_10 (and_10_out, not_3_out, s_r_ff_7_q);
  or or_12 (or_12_out, shift_register_1_p1, s_r_ff_7_qn);
  Counter #(.max('hffffff), .width(24)) counter_3 (
    .clr(or_12_out), .load(and_9_out), .up(1'b1), .count(and_10_out), .clk(shift_register_1_p4),
    .D(controlled_buffer_1_out[31:8]), .carry(counter_3_carry), .Q(counter_3_q));
  ROM #(.addrWidth(24), .dataWidth(36)) Interupt_X1 (.addr(counter_3_q), .data(Interupt_X1_data));
  RAM #(.addrWidth(24), .clearpin("true"), .dataWidth(32)) ram_1 (
    .addr(RAM_Addr_q[23:0]), .we(decoder_6_out1[5]), .oe(decoder_5_out1[5]), .clk(shift_register_1_p4),
    .din(controlled_buffer_6_out[31:0]), .dout(ram_1_dout), .clr(shift_register_1_p1));
  or or_13 (or_13_out, or_17_out, s_r_ff_6_q);
  S_R_Flip_Flop s_r_ff_6 (
    .S(pull_resistor_7_node[1]), .clk(pull_resistor_7_node[1]), .Q(s_r_ff_6_q), .reset(or_23_out[1]));  // open: R, Qn, preset
  S_R_Flip_Flop s_r_ff_7 (
    .S(or_23_out[1]), .R(1'b0), .clk(or_23_out[1]), .Q(s_r_ff_7_q), .reset(counter_3_carry), .Qn(s_r_ff_7_qn));  // open: preset
  Pull_Resistor pull_resistor_12 (.node({decoder_6_out1[11:7], controlled_buffer_6_out[32], decoder_6_out1[5:0]}));
  not not_4 (not_4_out, s_r_ff_7_q);
  or or_14 (or_14_out, or_18_out, s_r_ff_9_q);
  assign controlled_buffer_3_out = s_r_ff_7_q ? Interupt_X1_data : 36'bz;  // Controlled_Buffer controlled_buffer_7
  BufferedRegister Deposit (
    .Q(controlled_buffer_6_out[31:0]), .Data(controlled_buffer_6_out[31:0]), .WriteEnable(decoder_6_out1[0]),
    .Clock(shift_register_1_p4), .Reset(or_15_out), .OuputEnable(decoder_5_out1[0]));
  or or_15 (or_15_out, and_5_out, shift_register_1_p1);
  BufferedRegister RegA (
    .Q(controlled_buffer_6_out[31:0]), .Data(controlled_buffer_6_out[31:0]), .WriteEnable(decoder_6_out1[1]),
    .Clock(shift_register_1_p4), .Reset(shift_register_1_p1), .OuputEnable(decoder_5_out1[1]));
  BufferedRegister RegB (
    .Q(controlled_buffer_6_out[31:0]), .Data(controlled_buffer_6_out[31:0]), .WriteEnable(decoder_6_out1[2]),
    .Clock(shift_register_1_p4), .Reset(shift_register_1_p1), .OuputEnable(decoder_5_out1[2]));
  BufferedRegister RegC (
    .Q(controlled_buffer_6_out[31:0]), .Data(controlled_buffer_6_out[31:0]), .WriteEnable(decoder_6_out1[3]),
    .Clock(shift_register_1_p4), .Reset(shift_register_1_p1), .OuputEnable(decoder_5_out1[3]));
  BufferedRegister RegD (
    .Q(controlled_buffer_6_out[31:0]), .Data(controlled_buffer_6_out[31:0]), .WriteEnable(decoder_6_out1[4]),
    .Clock(shift_register_1_p4), .Reset(shift_register_1_p1), .OuputEnable(decoder_5_out1[4]));
  assign controlled_buffer_6_out[31:0] = decoder_5_out1[5] ? ram_1_dout : 32'bz;  // Controlled_Buffer controlled_buffer_8
  // PortIO #(.direction("onlyOutput"), .number(33)) portio_1: pin names not known
  and and_11 (and_11_out, pull_resistor_2_node, or_23_out[2]);
  and and_12 (and_12_out, not_4_out, s_r_ff_9_q);
  or or_16 (or_16_out, shift_register_1_p1, s_r_ff_9_qn);
  Counter #(.max('hffffff), .width(24)) counter_4 (
    .clr(or_16_out), .load(and_11_out), .up(1'b1), .count(and_12_out), .clk(shift_register_1_p4),
    .D(controlled_buffer_1_out[31:8]), .carry(counter_4_carry), .Q(counter_4_q));
  ROM #(.addrWidth(24), .dataWidth(36)) Interupt_X2 (.addr(counter_4_q), .data(Interupt_X2_data));
  Pull_Resistor pull_resistor_13 (.node(shift_register_1_p1));
  Pull_Resistor pull_resistor_14 (.node(controlled_buffer_6_out[32]));
  or or_17 (or_17_out, or_20_out, s_r_ff_8_q);
  S_R_Flip_Flop s_r_ff_8 (
    .S(pull_resistor_7_node[2]), .clk(pull_resistor_7_node[2]), .Q(s_r_ff_8_q), .reset(or_23_out[2]));  // open: R, Qn, preset
  S_R_Flip_Flop s_r_ff_9 (
    .S(or_23_out[2]), .R(1'b0), .clk(or_23_out[2]), .Q(s_r_ff_9_q), .reset(counter_4_carry), .Qn(s_r_ff_9_qn));  // open: preset
  not not_5 (not_5_out, s_r_ff_9_q);
  Pull_Resistor pull_resistor_15 (.node(decoder_5_out1[6]));
  Controlled_Buffer #(.width(32)) controlled_buffer_9 (
    .out(controlled_buffer_6_out[31:0]), .en(decoder_5_out1[6]));  // open: in
  // PortIO #(.direction("onlyinput"), .number(32)) portio_2: pin names not known
  or or_18 (or_18_out, or_21_out, s_r_ff_11_q);
  assign controlled_buffer_3_out = s_r_ff_9_q ? Interupt_X2_data : 36'bz;  // Controlled_Buffer controlled_buffer_10
  and and_13 (and_13_out, pull_resistor_2_node, or_23_out[3]);
  and and_14 (and_14_out, not_5_out, s_r_ff_11_q);
  or or_19 (or_19_out, shift_register_1_p1, s_r_ff_11_qn);
  Counter #(.max('hffffff), .width(24)) counter_5 (
    .clr(or_19_out), .load(and_13_out), .up(1'b1), .count(and_14_out), .clk(shift_register_1_p4),
    .D(controlled_buffer_1_out[31:8]), .carry(counter_5_carry), .Q(counter_5_q));
  ROM #(.addrWidth(24), .dataWidth(36)) Interupt_X3 (.addr(counter_5_q), .data(Interupt_X3_data));
  or or_20 (or_20_out, s_r_ff_12_q, s_r_ff_10_q);
  S_R_Flip_Flop s_r_ff_10 (
    .S(pull_resistor_7_node[3]), .clk(pull_resistor_7_node[3]), .Q(s_r_ff_10_q), .reset(or_23_out[3]));  // open: R, Qn, preset
  S_R_Flip_Flop s_r_ff_11 (
    .S(or_23_out[3]), .R(1'b0), .clk(or_23_out[3]), .Q(s_r_ff_11_q), .reset(counter_5_carry),
    .Qn(s_r_ff_11_qn));  // open: preset
  not not_6 (not_6_out, s_r_ff_11_q);
  Register #(.width(32)) ALU_A (
    .D(controlled_buffer_6_out[31:0]), .en(decoder_6_out1[9]), .clk(shift_register_1_p4), .Q(ALU_A_q),
    .clr(shift_register_1_p1));
  Register #(.width(32)) ALU_B (
    .D(controlled_buffer_6_out[31:0]), .en(decoder_6_out1[10]), .clk(shift_register_1_p4), .Q(ALU_B_q),
    .clr(shift_register_1_p1));
  Register #(.width(32)) ALU_C (
    .D(controlled_buffer_6_out[31:0]), .en(decoder_6_out1[11]), .clk(shift_register_1_p4), .Q(ALU_C_q),
    .clr(shift_register_1_p1));
  buf or_21 (or_21_out, s_r_ff_13_q);  // OR_Gate
  assign controlled_buffer_3_out = s_r_ff_11_q ? Interupt_X3_data : 36'bz;  // Controlled_Buffer controlled_buffer_11
  and and_15 (and_15_out, pull_resistor_2_node, or_23_out[4]);
  and and_16 (and_16_out, not_6_out, s_r_ff_13_q);
  or or_22 (or_22_out, shift_register_1_p1, s_r_ff_13_qn);
  Counter #(.max('hffffff), .width(24)) counter_6 (
    .clr(or_22_out), .load(and_15_out), .up(1'b1), .count(and_16_out), .clk(shift_register_1_p4),
    .D(controlled_buffer_1_out[31:8]), .carry(counter_6_carry), .Q(counter_6_q));
  ROM #(.addrWidth(24), .dataWidth(36)) Interupt_X4 (.addr(counter_6_q), .data(Interupt_X4_data));
  ALU alu_1 (
    .OutA(alu_1_outa), .OutB(alu_1_outb), .A(ALU_A_q), .B(ALU_B_q), .C(ALU_C_q),
    .Mode(stateregister_1_q[19:16]));
  S_R_Flip_Flop s_r_ff_12 (
    .S(pull_resistor_7_node[4]), .clk(pull_resistor_7_node[4]), .Q(s_r_ff_12_q), .reset(or_23_out[4]));  // open: R, Qn, preset
  S_R_Flip_Flop s_r_ff_13 (
    .S(or_23_out[4]), .R(1'b0), .clk(or_23_out[4]), .Q(s_r_ff_13_q), .reset(counter_6_carry),
    .Qn(s_r_ff_13_qn));  // open: preset
  BufferedRegister ALU_OA (
    .Q({ALU_OA_q[30:1], ALU_OA_q_2[1], ALU_OA_q[0]}), .Data(alu_1_outa), .WriteEnable(1'b1),
    .Clock(shift_register_1_p4), .Reset(shift_register_1_p1), .OuputEnable(decoder_5_out1[8]));
  assign controlled_buffer_6_out[31:0] = {ALU_OA_q[30:1], ALU_OA_q_2[1], ALU_OA_q[0]};  // Buffer buffer_1, 32 bits wide
  BufferedRegister ALU_OB (
    .Q(controlled_buffer_6_out[31:0]), .Data(alu_1_outb), .WriteEnable(1'b1), .Clock(shift_register_1_p4),
    .Reset(shift_register_1_p1), .OuputEnable(decoder_5_out1[9]));
  assign or_23_out = demultiplexer_2_out1 | pull_resistor_16_node;  // OR_Gate or_23, 5 bits wide
  assign controlled_buffer_3_out = s_r_ff_13_q ? Interupt_X4_data : 36'bz;  // Controlled_Buffer controlled_buffer_12
  D_Flip_Flop d_ff_1 (.D(demultiplexer_1_out6[0]), .clk(decoder_2_out6));  // open: Q, Qn, preset, reset
  Pull_Resistor pull_resistor_16 (.node(pull_resistor_16_node[0]));
  Pull_Resistor pull_resistor_17 (.node(pull_resistor_16_node[4:1]));
  // PortIO #(.direction("onlyinput"), .number(4)) portio_3: pin names not known; wires that end beside it: pull_resistor_16_node[4:1]
  FrameGraphics framegraphics_1 ();  // open: RefreshScreen, Reset, VRAM_Address, Write_VRAM, Clock, PixelData, ScreenClock, Writing, Clear, X, Y, Color

  // Notes on the sheet:
  //   contents of rom_1 (hex, n*v repeats v):
  //   0 2c0a000000000000 1056070481410200 30d1042000000000 3040000000000000 3080000000000000
  //   204a000000000000 3100000000000000 4049090618000000 5151201620000000 7400000000000000
  //   6400000000000000 5400000000000000
  //   Clock Bus
  //   contents of Main (hex, n*v repeats v):
  //   0 3000000af 100000025 300000006 400000001 100000026 600000002 f00000000
  //   Argument Bus
  //   Data Bus
endmodule

module BufferedRegister (
  input  [31:0] Data,
  input  WriteEnable,
  input  Clock,
  input  Reset,
  input  OuputEnable,
  output [31:0] Q
);

  wire or_1_out, por_1_out;
  wire [31:0] register_1_q;

  POR por_1 (.out(por_1_out));
  Register #(.trigger("falling"), .width(32)) register_1 (
    .D(Data), .en(WriteEnable), .clk(Clock), .Q(register_1_q), .clr(or_1_out));
  or or_1 (or_1_out, Reset, por_1_out);
  assign Q = OuputEnable ? register_1_q : 32'bz;  // Controlled_Buffer controlled_buffer_1
endmodule

module ALU (
  input  [31:0] A,
  input  [31:0] B,
  input  [31:0] C,
  input  [3:0] Mode,
  output [31:0] OutA,
  output [31:0] OutB
);

  wire decoder_1_out0, decoder_1_out1, decoder_1_out2, decoder_1_out3, decoder_1_out4, decoder_1_out5,
       decoder_1_out6, decoder_1_out7, decoder_1_out8, decoder_1_out9, decoder_1_out10, decoder_1_out11,
       decoder_1_out12, decoder_1_out13, decoder_1_out14, decoder_1_out15;
  wire [0:0] adder_1_cout, bitfinder_1_found, bitfinder_2_found, bitfinder_3_found, bitfinder_4_found,
       subtractor_1_bout;
  wire [2:0] comparator_1_gt;
  wire [4:0] bitfinder_1_index, bitfinder_2_index, bitfinder_3_index, bitfinder_4_index;
  wire [6:0] bitadder_1_out;
  wire [26:0] pull_resistor_2_node;
  wire [30:0] pull_resistor_1_node;
  wire [31:0] adder_1_out, divider_1_out, divider_1_rem, multiplier_1_cout, multiplier_1_out, negator_1_out,
       shifter_1_out, shifter_2_out, shifter_3_out, shifter_4_out, shifter_5_out, subtractor_1_out;

  Pull_Resistor pull_resistor_1 (.node(pull_resistor_1_node));
  Pull_Resistor pull_resistor_2 (.node(pull_resistor_2_node));
  Pull_Resistor pull_resistor_3 (.node(A));
  Pull_Resistor pull_resistor_4 (.node(B));
  Pull_Resistor pull_resistor_5 (.node(C));
  Adder #(.width(32)) adder_1 (.a(A), .b(B), .out(adder_1_out), .cin(C[0]), .cout(adder_1_cout[0]));
  Subtractor #(.width(32)) subtractor_1 (.a(A), .b(B), .out(subtractor_1_out), .bin(C[0]), .bout(subtractor_1_bout[0]));
  Multiplier #(.mode("twosComplement"), .width(32)) multiplier_1 (
    .a(A), .b(B), .out(multiplier_1_out), .cin(C), .cout(multiplier_1_cout));
  Divider #(.mode("twosComplement"), .width(32)) divider_1 (
    .a(A), .b(B), .out(divider_1_out), .upper(C), .rem(divider_1_rem));
  Negator #(.width(32)) negator_1 (.in(A), .out(negator_1_out));
  Comparator #(.width(32)) comparator_1 (
    .a(A), .b(B), .gt(comparator_1_gt[0]), .eq(comparator_1_gt[1]), .lt(comparator_1_gt[2]));
  Shifter #(.width(32)) shifter_1 (.in(A), .\dist (B[4:0]), .out(shifter_1_out));
  Shifter #(.shift("lr"), .width(32)) shifter_2 (.in(A), .\dist (B[4:0]), .out(shifter_2_out));
  Shifter #(.shift("ar"), .width(32)) shifter_3 (.in(A), .\dist (B[4:0]), .out(shifter_3_out));
  Shifter #(.shift("rl"), .width(32)) shifter_4 (.in(A), .\dist (B[4:0]), .out(shifter_4_out));
  Shifter #(.shift("rr"), .width(32)) shifter_5 (.in(A), .\dist (B[4:0]), .out(shifter_5_out));
  BitAdder #(.width(32)) bitadder_1 (.in0(A), .in1(B), .in2(C), .out(bitadder_1_out));
  BitFinder #(.width(32)) bitfinder_1 (.in(A), .index(bitfinder_1_index), .found(bitfinder_1_found[0]));
  BitFinder #(.\type ("high1"), .width(32)) bitfinder_2 (
    .in(A), .index(bitfinder_2_index), .found(bitfinder_2_found[0]));
  BitFinder #(.\type ("low0"), .width(32)) bitfinder_3 (
    .in(A), .index(bitfinder_3_index), .found(bitfinder_3_found[0]));
  BitFinder #(.\type ("high0"), .width(32)) bitfinder_4 (
    .in(A), .index(bitfinder_4_index), .found(bitfinder_4_found[0]));
  Pull_Resistor pull_resistor_6 (.node(OutA));
  Pull_Resistor pull_resistor_7 (.node(OutB));
  assign OutA = decoder_1_out0 ? adder_1_out : 32'bz;  // Controlled_Buffer controlled_buffer_1
  assign OutB = decoder_1_out0 ? {C[31:1], adder_1_cout[0]} : 32'bz;  // Controlled_Buffer controlled_buffer_2
  assign OutA = decoder_1_out1 ? subtractor_1_out : 32'bz;  // Controlled_Buffer controlled_buffer_3
  assign OutB = decoder_1_out1 ? {C[31:1], subtractor_1_bout[0]} : 32'bz;  // Controlled_Buffer controlled_buffer_4
  assign OutA = decoder_1_out2 ? multiplier_1_out : 32'bz;  // Controlled_Buffer controlled_buffer_5
  assign OutB = decoder_1_out2 ? multiplier_1_cout : 32'bz;  // Controlled_Buffer controlled_buffer_6
  assign OutA = decoder_1_out3 ? divider_1_out : 32'bz;  // Controlled_Buffer controlled_buffer_7
  assign OutB = decoder_1_out3 ? divider_1_rem : 32'bz;  // Controlled_Buffer controlled_buffer_8
  assign OutA = decoder_1_out4 ? negator_1_out : 32'bz;  // Controlled_Buffer controlled_buffer_9
  assign OutA = decoder_1_out5 ? {{29{1'b0}}, comparator_1_gt} : 32'bz;  // Controlled_Buffer controlled_buffer_10
  assign OutA = decoder_1_out6 ? shifter_1_out : 32'bz;  // Controlled_Buffer controlled_buffer_11
  assign OutA = decoder_1_out7 ? shifter_2_out : 32'bz;  // Controlled_Buffer controlled_buffer_12
  assign OutA = decoder_1_out8 ? shifter_3_out : 32'bz;  // Controlled_Buffer controlled_buffer_13
  assign OutA = decoder_1_out9 ? shifter_4_out : 32'bz;  // Controlled_Buffer controlled_buffer_14
  assign OutA = decoder_1_out10 ? shifter_5_out : 32'bz;  // Controlled_Buffer controlled_buffer_15
  assign OutA = decoder_1_out11 ? {{25{1'b0}}, bitadder_1_out} : 32'bz;  // Controlled_Buffer controlled_buffer_16
  assign OutA = decoder_1_out12 ? {pull_resistor_2_node, bitfinder_1_index} : 32'bz;  // Controlled_Buffer controlled_buffer_17
  assign OutB = decoder_1_out12 ? {pull_resistor_1_node, bitfinder_1_found[0]} : 32'bz;  // Controlled_Buffer controlled_buffer_18
  assign OutA = decoder_1_out13 ? {pull_resistor_2_node, bitfinder_2_index} : 32'bz;  // Controlled_Buffer controlled_buffer_19
  assign OutB = decoder_1_out13 ? {pull_resistor_1_node, bitfinder_2_found[0]} : 32'bz;  // Controlled_Buffer controlled_buffer_20
  assign OutA = decoder_1_out14 ? {pull_resistor_2_node, bitfinder_3_index} : 32'bz;  // Controlled_Buffer controlled_buffer_21
  assign OutB = decoder_1_out14 ? {pull_resistor_1_node, bitfinder_3_found[0]} : 32'bz;  // Controlled_Buffer controlled_buffer_22
  assign OutA = decoder_1_out15 ? {pull_resistor_2_node, bitfinder_4_index} : 32'bz;  // Controlled_Buffer controlled_buffer_23
  assign OutB = decoder_1_out15 ? {pull_resistor_1_node, bitfinder_4_found[0]} : 32'bz;  // Controlled_Buffer controlled_buffer_24
  Decoder #(.enable("false"), .select(4)) decoder_1 (
    .out0(decoder_1_out0), .out1(decoder_1_out1), .out2(decoder_1_out2), .out3(decoder_1_out3),
    .out4(decoder_1_out4), .out5(decoder_1_out5), .out6(decoder_1_out6), .out7(decoder_1_out7),
    .out8(decoder_1_out8), .out9(decoder_1_out9), .out10(decoder_1_out10), .out11(decoder_1_out11),
    .out12(decoder_1_out12), .out13(decoder_1_out13), .out14(decoder_1_out14), .out15(decoder_1_out15),
    .sel(Mode));
  // also tied to GND on the sheet: {C[1], C[2], C[3], C[4], C[5], C[6], C[7], C[8], C[9], C[10], C[11], C[12], C[13], C[14], C[15], C[16], C[17], C[18], C[19], C[20], C[21], C[22], C[23], C[24], C[25], C[26], C[27], C[28], C[29], C[30], C[31]}
endmodule

module StateRegister (
  input  [19:0] Data,
  input  [4:0] Selector,
  input  Clock,
  input  Reset,
  output [19:0] Q
);

  wire not_1_out, not_2_out, not_3_out, not_4_out, not_5_out;
  wire [3:0] register_1_q, register_2_q, register_3_q, register_4_q, register_5_q;

  assign Q[3:0] = Selector[0] ? Data[3:0] : 4'bz;  // Controlled_Buffer controlled_buffer_1
  Register #(.trigger("falling"), .width(4)) register_1 (
    .D(Data[3:0]), .en(Selector[0]), .clk(Clock), .Q(register_1_q), .clr(Reset));
  assign Q[7:4] = Selector[1] ? Data[7:4] : 4'bz;  // Controlled_Buffer controlled_buffer_2
  Register #(.trigger("falling"), .width(4)) register_2 (
    .D(Data[7:4]), .en(Selector[1]), .clk(Clock), .Q(register_2_q), .clr(Reset));
  assign Q[11:8] = Selector[2] ? Data[11:8] : 4'bz;  // Controlled_Buffer controlled_buffer_3
  Register #(.trigger("falling"), .width(4)) register_3 (
    .D(Data[11:8]), .en(Selector[2]), .clk(Clock), .Q(register_3_q), .clr(Reset));
  assign Q[15:12] = Selector[3] ? Data[15:12] : 4'bz;  // Controlled_Buffer controlled_buffer_4
  Register #(.trigger("falling"), .width(4)) register_4 (
    .D(Data[15:12]), .en(Selector[3]), .clk(Clock), .Q(register_4_q), .clr(Reset));
  assign Q[19:16] = Selector[4] ? Data[19:16] : 4'bz;  // Controlled_Buffer controlled_buffer_5
  Register #(.trigger("falling"), .width(4)) register_5 (
    .D(Data[19:16]), .en(Selector[4]), .clk(Clock), .Q(register_5_q), .clr(Reset));
  not not_1 (not_1_out, Selector[0]);
  assign Q[3:0] = not_1_out ? register_1_q : 4'bz;  // Controlled_Buffer controlled_buffer_6
  not not_2 (not_2_out, Selector[1]);
  assign Q[7:4] = not_2_out ? register_2_q : 4'bz;  // Controlled_Buffer controlled_buffer_7
  not not_3 (not_3_out, Selector[2]);
  assign Q[11:8] = not_3_out ? register_3_q : 4'bz;  // Controlled_Buffer controlled_buffer_8
  not not_4 (not_4_out, Selector[3]);
  assign Q[15:12] = not_4_out ? register_4_q : 4'bz;  // Controlled_Buffer controlled_buffer_9
  not not_5 (not_5_out, Selector[4]);
  assign Q[19:16] = not_5_out ? register_5_q : 4'bz;  // Controlled_Buffer controlled_buffer_10
endmodule

module RisingEdgeTrigger (
  input  in_1,
  output out_2
);

  wire and_1_out, not_1_out, s_r_ff_1_q;

  S_R_Flip_Flop s_r_ff_1 (.Q(s_r_ff_1_q), .reset(out_2), .preset(not_1_out));  // open: S, R, clk, Qn
  not not_1 (not_1_out, in_1);
  S_R_Flip_Flop s_r_ff_2 (.S(and_1_out), .R(1'b0), .clk(and_1_out), .Q(out_2), .reset(out_2));  // open: Qn, preset
  and and_1 (and_1_out, s_r_ff_1_q, in_1);
endmodule
